// Logisim project goatedCPU.circ as structural Verilog: 1 circuit, main circuit main
module main (
  input  Reset
);

  wire ADD_out, and_1_out, and_2_out, and_3_out, and_4_out, and_5_out, and_6_out, clock_1_out, clock_2_out,
       decoder_1_out0, decoder_1_out1, decoder_1_out2, decoder_1_out3, LDR_out, not_1_out, not_2_out,
       not_3_out, not_4_out, not_5_out, not_6_out, not_7_out, STR_out, SUB_out;
  wire [0:0] not_8_out;
  wire [1:0] InstructionMemory_dout_3, InstructionMemory_dout_4, multiplexer_2_out;
  wire [7:0] adder_1_out, adder_2_out, DataMemory_dout, InstructionMemory_dout_2, multiplexer_1_out,
       multiplexer_3_out, multiplexer_4_out, multiplexer_5_out, multiplexer_6_out, multiplexer_7_out, PC_q,
       subtractor_1_out, X0_q, X1_q, X2_q, X3_q;
  wire [15:2] InstructionMemory_dout;

  Clock clock_1 (.out(clock_1_out));
  and and_1 (and_1_out, not_8_out[0], clock_1_out);
  not not_1 (not_1_out, Reset);
  and STR (STR_out, InstructionMemory_dout[15], not_8_out[0], InstructionMemory_dout[14]);
  LED led_1 (.in(STR_out));
  Register #(.trigger("falling")) PC (.D(adder_1_out), .en(not_1_out), .clk(and_1_out), .Q(PC_q), .clr(Reset));
  Adder adder_1 (.a(PC_q), .b({{7{1'b0}}, not_8_out[0]}), .out(adder_1_out));  // open: cin, cout
  not not_2 (not_2_out, InstructionMemory_dout[14]);
  not not_3 (not_3_out, InstructionMemory_dout[15]);
  and LDR (LDR_out, InstructionMemory_dout[15], not_2_out);
  LED led_2 (.in(LDR_out));
  not not_4 (not_4_out, InstructionMemory_dout[15]);
  and SUB (SUB_out, not_3_out, InstructionMemory_dout[14]);
  and ADD (ADD_out, not_4_out, not_6_out);
  LED led_3 (.in(SUB_out));
  LED led_4 (.in(ADD_out));
  not not_5 (not_5_out, STR_out);
  not not_6 (not_6_out, InstructionMemory_dout[14]);
  Decoder #(.select(2)) decoder_1 (
    .out0(decoder_1_out0), .out1(decoder_1_out1), .out2(decoder_1_out2), .out3(decoder_1_out3),
    .sel(InstructionMemory_dout_3));  // open: en
  RAM #(.dataWidth(16)) InstructionMemory (
    .addr(PC_q), .we(1'b0), .oe(not_1_out), .clk(clock_2_out),
    .dout({InstructionMemory_dout[15:14], InstructionMemory_dout_2, InstructionMemory_dout[5], InstructionMemory_dout_3, InstructionMemory_dout[2], InstructionMemory_dout_4}));  // open: din
  Clock clock_2 (.out(clock_2_out));
  not not_7 (not_7_out, STR_out);
  RAM #(.asyncread("true")) DataMemory (
    .addr(multiplexer_7_out), .we(STR_out), .oe(not_5_out), .clk(and_1_out), .din(multiplexer_4_out),
    .dout(DataMemory_dout));
  Register X0 (.D(multiplexer_1_out), .en(and_2_out), .clk(and_1_out), .Q(X0_q), .clr(Reset));
  and and_2 (and_2_out, decoder_1_out0, not_7_out);
  Register X1 (.D(multiplexer_1_out), .en(and_3_out), .clk(and_1_out), .Q(X1_q), .clr(Reset));
  and and_3 (and_3_out, decoder_1_out1, not_7_out);
  Register X2 (.D(multiplexer_1_out), .en(and_4_out), .clk(and_1_out), .Q(X2_q), .clr(Reset));
  and and_4 (and_4_out, decoder_1_out2, not_7_out);
  Register X3 (.D(multiplexer_1_out), .en(and_5_out), .clk(and_1_out), .Q(X3_q), .clr(Reset));
  and and_5 (and_5_out, decoder_1_out3, not_7_out);
  Multiplexer #(.width(8)) multiplexer_1 (
    .in0(multiplexer_7_out), .in1(DataMemory_dout), .out(multiplexer_1_out), .sel(LDR_out));
  Multiplexer #(.width(2)) multiplexer_2 (
    .in0({InstructionMemory_dout_2[0], InstructionMemory_dout[5]}), .in1(InstructionMemory_dout_3),
    .out(multiplexer_2_out), .sel(InstructionMemory_dout[2]));
  Multiplexer #(.select(2), .width(8)) multiplexer_3 (
    .in0(X0_q), .in1(X1_q), .in2(X2_q), .in3(X3_q), .out(multiplexer_3_out), .sel(InstructionMemory_dout_4));
  Multiplexer #(.select(2), .width(8)) multiplexer_4 (
    .in0(X0_q), .in1(X1_q), .in2(X2_q), .in3(X3_q), .out(multiplexer_4_out), .sel(InstructionMemory_dout_3));
  Multiplexer #(.select(2), .width(8)) multiplexer_5 (
    .in0(X0_q), .in1(X1_q), .in2(X2_q), .in3(X3_q), .out(multiplexer_5_out), .sel(multiplexer_2_out));
  not not_8 (not_8_out[0], and_6_out);
  and and_6 (and_6_out, InstructionMemory_dout_2[1], InstructionMemory_dout_4[0], InstructionMemory_dout_4[1], InstructionMemory_dout[2], InstructionMemory_dout_3[0], InstructionMemory_dout_3[1], InstructionMemory_dout[5], InstructionMemory_dout_2[0], InstructionMemory_dout_2[2], InstructionMemory_dout_2[3], InstructionMemory_dout_2[4], InstructionMemory_dout_2[5], InstructionMemory_dout_2[6], InstructionMemory_dout_2[7], InstructionMemory_dout[14], InstructionMemory_dout[15]);
  Multiplexer #(.width(8)) multiplexer_6 (
    .in0(multiplexer_5_out), .in1(InstructionMemory_dout_2), .out(multiplexer_6_out),
    .sel(InstructionMemory_dout[2]));
  Adder adder_2 (.a(multiplexer_6_out), .b(multiplexer_3_out), .out(adder_2_out));  // open: cin, cout
  Subtractor subtractor_1 (.a(multiplexer_3_out), .b(multiplexer_6_out), .out(subtractor_1_out));  // open: bin, bout
  Multiplexer #(.width(8)) multiplexer_7 (
    .in0(adder_2_out), .in1(subtractor_1_out), .out(multiplexer_7_out), .sel(SUB_out));

  // Notes on the sheet:
  //   Kazi Tishan
  //   CPU name: GoatedCPU
  //   I pledge my honor that I have abided by the Stevens Honor System
  //   MemWrite
  //   MemRead
  //   WriteReg
  //   WriteEnable
  //   ALUout
  //   ReadDataM
  //   Imm
  //   RegDataW
  //   ReadReg1
  //   ReadReg2
  //   RegData1
  //   WriteDataM
  //   RegData2
  //   Imm?
  //   ALUout
endmodule
